# Fritzing sketch Ultrasonic-Alarm-System (saved by Fritzing 0.9.3b)
breadboards: 1

parts:
  Part1 = Arduino Uno (Rev3) - ICSP
  hc-sr1 = hc-sr04
  LCD1 = LCD screen
  S1 = Pushbutton [package="[SMD]"]
  S2 = Pushbutton [package="[SMD]"]
  S3 = Pushbutton [package="[SMD]"]
  S4 = Pushbutton [package="[SMD]"]

nets:
  N1: Part1.ICSP_MISO, Part1.D12/MISO, LCD1.DB7
  N2: Part1.D8, LCD1.E
  N3: Part1.D9_PWM, LCD1.DB4
  N4: Part1.D10_PWM/SS, LCD1.DB5
  N5: Part1.D11_PWM/MOSI, LCD1.DB6
  N6: Part1.D13/SCK, S4.Pin_3, S4.Pin_4
  N7: Part1.D2, S3.Pin_3, S3.Pin_4
  N8: Part1.D3_PWM, S2.Pin_3, S2.Pin_4
  N9: Part1.D4, S1.Pin_3, S1.Pin_4
  N10: Part1.D5_PWM, hc-sr1.Echo
  N11: Part1.D6_PWM, hc-sr1.Trig
  N12: Part1.D7, LCD1.RS
  5V: Part1.5V, hc-sr1.VCC, LCD1.VDD, LCD1.LED+
  GND: Part1.GND, hc-sr1.GND, LCD1.VSS, LCD1.V0, LCD1.R/W, LCD1.LED-, S1.Pin_1, S1.Pin_2, S2.Pin_1, S2.Pin_2, S3.Pin_1, S3.Pin_2, S4.Pin_1, S4.Pin_2
